// Logisim project Control Unit.circ as structural Verilog: 2 circuits, main circuit Instruction decoder
module main (
  input  [31:0] Instruction,
  input  [1:0] Flags,
  input  RT_WT_latencies,
  output [4:0] Rs,
  output [4:0] Rt,
  output [1:0] Sp_op,
  output [1:0] Pc_op,
  output [15:0] Const,
  output [2:0] Alu_op,
  output [25:0] Jump,
  output [4:0] Register_write_addres,
  output Const_enable,
  output Const_op,
  output Hi_Lo_enable,
  output Hi_Lo_register_read,
  output Mult_div_enable,
  output [1:0] Mult_div_op,
  output Register_write_enable,
  output Immediate_value_enable
);

  wire _000000, _111000, _111111, ADD, ADD_out, ADDI, AND, AND_11_out, and_15_out, and_16_out, and_17_out,
       and_18_out, and_19_out, and_20_out, and_21_out, ANDI, BEQ, BGTZ, BLEZ, BLTZ, BNE, comparator_1_eq,
       comparator_2_eq, comparator_3_eq, comparator_6_eq, comparator_10_eq, comparator_11_eq,
       comparator_12_eq, comparator_15_eq, comparator_16_eq, comparator_19_eq, comparator_20_eq,
       comparator_23_eq, comparator_24_eq, comparator_26_eq, comparator_27_eq, comparator_29_eq,
       comparator_31_eq, comparator_32_eq, comparator_34_eq, comparator_37_eq, comparator_38_eq,
       comparator_39_eq, DIV, DIVU, HALT, J, JR, KBD, LW, MFHI, MFLO, MULT, MULU, NOP, NOR, OR, or_2_out,
       or_3_out, or_4_out, or_5_out, or_6_out, or_8_out, OR_out, ORI, POP, priority_encoder_1_en_out,
       priority_encoder_2_en_out, priority_encoder_3_en_out, priority_encoder_3_out,
       priority_encoder_4_en_out, priority_encoder_4_out, priority_encoder_5_en_out,
       priority_encoder_6_en_out, PUSH, RND, SLT, SLT_out, SLTI, SLTIU, SLTU, SLTU_out, SUB, SUB_out, SW,
       TTY, XOR, XOR_out, XORI;
  wire [1:0] priority_encoder_1_out, priority_encoder_5_out, priority_encoder_6_out;
  wire [2:0] priority_encoder_2_out;
  wire [4:0] RD;
  wire [5:0] FUNC, OP;

  Comparator #(.width(6), .mode("unsigned")) comparator_1 (
    .a(6'b100000), .b(FUNC), .eq(comparator_1_eq));  // open: gt, lt
  Comparator #(.width(6), .mode("unsigned")) comparator_2 (
    .a(6'b100100), .b(FUNC), .eq(comparator_2_eq));  // open: gt, lt
  Comparator #(.width(6), .mode("unsigned")) comparator_3 (
    .a(6'b101010), .b(FUNC), .eq(comparator_3_eq));  // open: gt, lt
  Comparator #(.width(6), .mode("unsigned")) comparator_4 (.a(6'b000100), .b(OP), .eq(BEQ));  // open: gt, lt
  Comparator #(.width(6), .mode("unsigned")) comparator_5 (.a(6'b100011), .b(OP), .eq(LW));  // open: gt, lt
  Comparator #(.width(6), .mode("unsigned")) comparator_6 (
    .a(6'b000100), .b(FUNC), .eq(comparator_6_eq));  // open: gt, lt
  and and_1 (SLT, _000000, comparator_3_eq);
  and and_2 (ADD, _000000, comparator_1_eq);
  and and_3 (AND, _000000, comparator_2_eq);
  and and_4 (KBD, _111111, comparator_6_eq);
  Comparator #(.width(6)) comparator_7 (.a(OP), .b({6{1'b0}}), .eq(_000000));  // open: gt, lt
  Comparator #(.width(6)) comparator_8 (.a(OP), .b(6'b111000), .eq(_111000));  // open: gt, lt
  Comparator #(.width(6)) comparator_9 (.a(OP), .b({6{1'b1}}), .eq(_111111));  // open: gt, lt
  Instruction_decoder instruction_decoder_1 (
    .Instruction(Instruction), .FUNC_CODE(FUNC), .OP_CODE(OP), .RS(Rs), .RT(Rt), .RD(RD), .JUMP(Jump),
    .CONST(Const));
  Comparator #(.width(6), .mode("unsigned")) comparator_10 (
    .a(6'b100010), .b(FUNC), .eq(comparator_10_eq));  // open: gt, lt
  Comparator #(.width(6), .mode("unsigned")) comparator_11 (
    .a(6'b100101), .b(FUNC), .eq(comparator_11_eq));  // open: gt, lt
  Comparator #(.width(6), .mode("unsigned")) comparator_12 (
    .a(6'b101011), .b(FUNC), .eq(comparator_12_eq));  // open: gt, lt
  Comparator #(.width(6), .mode("unsigned")) comparator_13 (.a(6'b000101), .b(OP), .eq(BNE));  // open: gt, lt
  Comparator #(.width(6), .mode("unsigned")) comparator_14 (.a(6'b101011), .b(OP), .eq(SW));  // open: gt, lt
  and and_5 (SUB, _000000, comparator_10_eq);
  and and_6 (OR, _000000, comparator_11_eq);
  and and_7 (SLTU, _000000, comparator_12_eq);
  Comparator #(.width(6), .mode("unsigned")) comparator_15 (
    .a(6'b011000), .b(FUNC), .eq(comparator_15_eq));  // open: gt, lt
  Comparator #(.width(6), .mode("unsigned")) comparator_16 (
    .a(6'b100111), .b(FUNC), .eq(comparator_16_eq));  // open: gt, lt
  Comparator #(.width(6), .mode("unsigned")) comparator_17 (.a(6'b001010), .b(OP), .eq(SLTI));  // open: gt, lt
  Comparator #(.width(6), .mode("unsigned")) comparator_18 (.a(6'b000110), .b(OP), .eq(BLEZ));  // open: gt, lt
  Comparator #(.width(6), .mode("unsigned")) comparator_19 (
    .a({6{1'b0}}), .b(FUNC), .eq(comparator_19_eq));  // open: gt, lt
  and and_8 (MULT, _000000, comparator_15_eq);
  and and_9 (NOR, _000000, comparator_16_eq);
  and and_10 (POP, _111000, comparator_19_eq);
  or u_ADD (ADD_out, ADD, ADDI, MFHI, PUSH, MFLO, LW, SW);
  or u_SUB (SUB_out, SUB, BEQ, BNE);
  or AND_11 (AND_11_out, AND, ANDI);
  or u_OR (OR_out, OR, ORI);
  or u_XOR (XOR_out, XOR, XORI);
  or u_SLT (SLT_out, SLT, SLTI);
  or u_SLTU (SLTU_out, SLTU, SLTIU);
  not not_1 (Mult_div_enable, priority_encoder_1_en_out);
  Priority_Encoder #(.select(2)) priority_encoder_1 (
    .in0(MULT), .in1(MULU), .in2(DIV), .in3(DIVU), .out(priority_encoder_1_out),
    .en_out(priority_encoder_1_en_out));  // open: gs, en_in
  Multiplexer #(.width(2), .enable("false")) multiplexer_1 (
    .in0(priority_encoder_1_out), .in1(2'b00), .out(Mult_div_op), .sel(priority_encoder_1_en_out));
  Comparator #(.width(6), .mode("unsigned")) comparator_20 (
    .a(6'b011001), .b(FUNC), .eq(comparator_20_eq));  // open: gt, lt
  Comparator #(.width(6), .mode("unsigned")) comparator_21 (.a(6'b001011), .b(OP), .eq(SLTIU));  // open: gt, lt
  Comparator #(.width(6), .mode("unsigned")) comparator_22 (.a(6'b000111), .b(OP), .eq(BGTZ));  // open: gt, lt
  Comparator #(.width(6), .mode("unsigned")) comparator_23 (
    .a(6'b101000), .b(FUNC), .eq(comparator_23_eq));  // open: gt, lt
  Comparator #(.width(6), .mode("unsigned")) comparator_24 (
    .a(6'b000001), .b(FUNC), .eq(comparator_24_eq));  // open: gt, lt
  Priority_Encoder priority_encoder_2 (
    .in0(ADD_out), .in1(SUB_out), .in2(AND_11_out), .in3(OR_out), .in4(NOR), .in5(XOR_out), .in6(SLT_out),
    .in7(SLTU_out), .out(priority_encoder_2_out), .en_out(priority_encoder_2_en_out));  // open: en_in, gs
  and and_12 (MULU, _000000, comparator_20_eq);
  and and_13 (XOR, _000000, comparator_23_eq);
  and and_14 (PUSH, _111000, comparator_24_eq);
  Multiplexer #(.width(3), .enable("false")) multiplexer_2 (
    .in0(priority_encoder_2_out), .in1(3'b000), .out(Alu_op), .sel(priority_encoder_2_en_out));
  not not_2 (Hi_Lo_enable, priority_encoder_3_en_out);
  Priority_Encoder #(.select(1)) priority_encoder_3 (
    .in0(MFHI), .in1(MFLO), .out(priority_encoder_3_out), .en_out(priority_encoder_3_en_out));  // open: gs, en_in
  Multiplexer #(.enable("false")) multiplexer_3 (
    .in0(priority_encoder_3_out), .in1(1'b0), .out(Hi_Lo_register_read), .sel(priority_encoder_3_en_out));
  or or_2 (or_2_out, Flags[1], Flags[0]);
  and and_15 (and_15_out, ~Flags[1], ~Flags[0]);  // AND_Gate
  and and_16 (and_16_out, Flags[1], ~Flags[0]);  // AND_Gate
  Comparator #(.width(6), .mode("unsigned")) comparator_25 (.a(6'b001100), .b(OP), .eq(ANDI));  // open: gt, lt
  and and_17 (and_17_out, BEQ, Flags[0]);
  and and_18 (and_18_out, ~Flags[0], BNE);  // AND_Gate
  and and_19 (and_19_out, BLEZ, or_2_out);
  Comparator #(.width(6), .mode("unsigned")) comparator_26 (
    .a(6'b011010), .b(FUNC), .eq(comparator_26_eq));  // open: gt, lt
  Comparator #(.width(6), .mode("unsigned")) comparator_27 (
    .a(6'b010000), .b(FUNC), .eq(comparator_27_eq));  // open: gt, lt
  Comparator #(.width(6), .mode("unsigned")) comparator_28 (.a(6'b000001), .b(OP), .eq(BLTZ));  // open: gt, lt
  and and_20 (and_20_out, BGTZ, and_15_out);
  and and_21 (and_21_out, BLTZ, and_16_out);
  or or_3 (or_3_out, ADDI, SLTI, SLTIU, LW, SW);
  or or_4 (or_4_out, ANDI, ORI, XORI);
  and and_22 (DIV, _000000, comparator_26_eq);
  and and_23 (MFHI, _000000, comparator_27_eq);
  Comparator #(.width(6), .mode("unsigned")) comparator_29 (
    .a({6{1'b1}}), .b(FUNC), .eq(comparator_29_eq));  // open: gt, lt
  and and_24 (HALT, _111111, comparator_29_eq);
  or or_5 (or_5_out, and_17_out, and_18_out, and_19_out, and_20_out, and_21_out);
  not not_3 (Const_enable, priority_encoder_4_en_out);
  Multiplexer #(.enable("false")) multiplexer_4 (
    .in0(priority_encoder_4_out), .in1(1'b0), .out(Const_op), .sel(priority_encoder_4_en_out));
  Priority_Encoder #(.select(1)) priority_encoder_4 (
    .in0(or_3_out), .in1(or_4_out), .out(priority_encoder_4_out), .en_out(priority_encoder_4_en_out));  // open: gs, en_in
  Multiplexer #(.width(2), .enable("false")) multiplexer_5 (
    .in0(priority_encoder_5_out), .in1(2'b00), .out(Pc_op), .sel(priority_encoder_5_en_out));
  Priority_Encoder #(.select(2)) priority_encoder_5 (
    .in1(or_5_out), .in2(J), .in3(JR), .out(priority_encoder_5_out), .en_out(priority_encoder_5_en_out));  // open: in0, gs, en_in
  Comparator #(.width(6), .mode("unsigned")) comparator_30 (.a(6'b001101), .b(OP), .eq(ORI));  // open: gt, lt
  Comparator #(.width(6), .mode("unsigned")) comparator_31 (
    .a(6'b011011), .b(FUNC), .eq(comparator_31_eq));  // open: gt, lt
  Comparator #(.width(6), .mode("unsigned")) comparator_32 (
    .a(6'b010010), .b(FUNC), .eq(comparator_32_eq));  // open: gt, lt
  Comparator #(.width(6), .mode("unsigned")) comparator_33 (.a(6'b000010), .b(OP), .eq(J));  // open: gt, lt
  Comparator #(.width(6), .mode("unsigned")) comparator_34 (
    .a(6'b000001), .b(FUNC), .eq(comparator_34_eq));  // open: gt, lt
  and and_25 (DIVU, _000000, comparator_31_eq);
  and and_26 (MFLO, _000000, comparator_32_eq);
  and and_27 (TTY, _111111, comparator_34_eq);
  or or_6 (or_6_out, ADDI, ANDI, ORI, XORI, SLTI, SLTIU, LW);
  Multiplexer #(.width(5), .enable("false")) multiplexer_6 (
    .in0(RD), .in1(Rt), .out(Register_write_addres), .sel(or_6_out));
  Multiplexer #(.width(2), .enable("false")) multiplexer_7 (
    .in0(priority_encoder_6_out), .in1(2'b00), .out(Sp_op), .sel(priority_encoder_6_en_out));
  Priority_Encoder #(.select(2)) priority_encoder_6 (
    .in1(POP), .in2(PUSH), .out(priority_encoder_6_out), .en_out(priority_encoder_6_en_out));  // open: in0, in3, gs, en_in
  Comparator #(.width(6), .mode("unsigned")) comparator_35 (.a(6'b001000), .b(OP), .eq(ADDI));  // open: gt, lt
  Comparator #(.width(6), .mode("unsigned")) comparator_36 (.a(6'b001110), .b(OP), .eq(XORI));  // open: gt, lt
  Comparator #(.width(6), .mode("unsigned")) comparator_37 (
    .a({6{1'b0}}), .b(FUNC), .eq(comparator_37_eq));  // open: gt, lt
  Comparator #(.width(6), .mode("unsigned")) comparator_38 (
    .a(6'b001000), .b(FUNC), .eq(comparator_38_eq));  // open: gt, lt
  or or_7 (Immediate_value_enable, LW, POP);
  and and_28 (JR, _000000, comparator_38_eq);
  Comparator #(.width(6), .mode("unsigned")) comparator_39 (
    .a(6'b000010), .b(FUNC), .eq(comparator_39_eq));  // open: gt, lt
  and and_29 (NOP, _000000, comparator_37_eq);
  and and_30 (RND, _111111, comparator_39_eq);
  or or_8 (or_8_out, Mult_div_enable, NOP, BEQ, BNE, BLEZ, PUSH, BGTZ, BLTZ, J, JR, SW);
  not not_4 (Register_write_enable, or_8_out);

  // Other names for the same wires on the sheet: ZERO_F = Flags[0]; SIGN_F = Flags[1]; INST[31:0] = Instruction;
  //   MULT_DIV_OPS = Mult_div_enable

  // Notes on the sheet:
  //   AND
  //   KBD
  //   ADD
  //   SLT
  //   BEQ
  //   LW
  //   OR
  //   SUB
  //   SLTU
  //   BNE
  //   SW
  //   memory interface
  //   MULT
  //   NOR
  //   SLTI
  //   BLEZ
  //   POP
  //   Alu Control
  //   Mult/Div unit Control
  //   MULU
  //   XOR
  //   SLTIU
  //   BGTZ
  //   PUSH
  //   DIV
  //   ANDI
  //   MFHI
  //   BLTZ
  //   HALT
  //   Branch Control
  //   Constant unit Control
  //   DIVU
  //   ORI
  //   MFLO
  //   J
  //   TTY
  //   Sp Control
  //   Register Control
  //   NOP
  //   JR
  //   ADDI
  //   XORI
  //   RND
endmodule

module Instruction_decoder (
  input  [31:0] Instruction,
  output [5:0] OP_CODE,
  output [4:0] RS,
  output [4:0] RT,
  output [4:0] RD,
  output [5:0] FUNC_CODE,
  output [25:0] JUMP,
  output [15:0] CONST
);


  assign CONST = Instruction[15:0];
  assign FUNC_CODE = Instruction[5:0];
  assign JUMP = Instruction[25:0];
  assign OP_CODE = Instruction[31:26];
  assign RD = Instruction[15:11];
  assign RS = Instruction[25:21];
  assign RT = Instruction[20:16];

  // Other names for the same wires on the sheet: INST[31:0] = Instruction
endmodule
